# Fritzing sketch home weather station (saved by Fritzing 1.0.6)
circuit board: 15.1716cm x 5.69662cm

parts:
  LCD1 = 2.8" SPI TFT Module [part_number=MSP2807]
  A1 = AHT2x module
  U1 = NodeMCU V3.0

nets:
  N1: LCD1.pin1, LCD1.pin8, A1.Pin_4, U1.3V3
  N2: LCD1.pin2, A1.Pin_3, U1.GND
  N3: LCD1.pin3, U1.D8
  N4: LCD1.pin4, U1.D3
  N5: LCD1.pin5, U1.D4
  N6: LCD1.pin6, U1.D7
  N7: LCD1.pin7, U1.D5
  N8: LCD1.pin9, U1.D6
  N9: A1.Pin_1, U1.D2
  N10: A1.Pin_2, U1.D1

custom parts:
  2.8" SPI TFT Module: A generic 2.8 inch LCD TFT 320x240 display with touchscreen and SD card slot. Uses the ILI9341 controller, like the Adafruit displays of this size uses.
  AHT2x module: AHT10 AHT20 AHT21 High Precision Digital Temperature and Humidity Sensor Measurement Module I2C Communication.
  NodeMCU V3.0: ESP8266 based NodeMCU
